# Fritzing sketch midterm Sketch (saved by Fritzing 1.0.2b)
breadboards: 1

parts:
  Part1 = 16 NeoPixel Ring [part_number=1463]
  OLED_I2C1 = OLED 128x64 I2C Monochrome Display
  U1 = ENCODER_RGB [package=encoder_led_2]
  A1 = Particle - Photon2
  Part2 = BME280 Breakout

nets:
  VDD: Part1.IN, OLED_I2C1.VDD, U1.+, A1.Pin_2, A1.Pin_19, A1.Pin_31, Part2.3.3V
  N1: Part1.VDD, A1.Pin_26
  GND: Part1.GND, OLED_I2C1.GND, U1.B#2, U1.C, U1.A, A1.Pin_4, A1.Pin_14, A1.Pin_15, A1.Pin_18, A1.Pin_30, Part2.GND
  N2: OLED_I2C1.SDA, A1.Pin_21, Part2.SDI/SDA
  N3: OLED_I2C1.SCK, A1.Pin_20, Part2.SCK/SCL
  N4: U1.R, A1.Pin_10
  N5: U1.G, A1.Pin_11
  N6: U1.SW, A1.Pin_13
  N7: U1.B#8, A1.Pin_12

custom parts:
  16 NeoPixel Ring: 16 ultra bright smart LED NeoPixels are arranged in a circle with 1.75" (44.5mm) outer diameter. The rings are 'chainable' - connect the output pin of one to the input pin of another. Use only one microcontroller pin to control as many as you can chain together! Each LED is addressable as the driver chip is inside the LED. Each one has ~18mA constant current drive so the color will be very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
  ENCODER_RGB: SparkFun RGB rotary Encoder
  Particle - Photon2: The Photon 2 is a microcontroller and Wi-Fi networking developed by particle. Features: 802.11a/b/g/n Wi-Fi, 2.4 GHz and 5 GHz Integrated PCB antenna Integrated U.FL connector for external antenna Integrated RF switch BLE 5 using same antenna as Wi-Fi Realtek RTL8721DM MCU ARM Cortex M33 CPU, 200 MHz 2048 KB (2 MB) user application maximum size 3072 KB (3 MB) of RAM available to user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
